# Fritzing sketch Clase 10 Sensor PIR HC-SR501 (saved by Fritzing 0.9.10b)
breadboards: 1

parts:
  PIR1 = PIR sensor
  LED1 = LED - 5mm [color="Blue (525nm)" current=0.030 package="5 mm [THT]"]
  U1 = ESP32-38PinWide [part_number=ESP32-38PinWide]

nets:
  VDD: PIR1.VDD, U1.VIN
  N1: LED1.cathode, U1.GND
  N2: LED1.anode, U1.GPIO23

notes:
  Pines:
  PIR = GPIO 22
  LED = GPIO 23

custom parts:
  ESP32-38PinWide: Generic 38-Pin ESP32 with wide format (only access to one side of pins on a breadboard) based on Stephen Lilley's HiLetgo ESP-WROOM-32 ESP32 ESP-32S Development Board.
